# Fritzing sketch AFbook (saved by Fritzing 0.9.3b)

parts:
  Raspberry_Pi_Zero1 = Raspberry Pi Zero
  SparkFun_Simultaneous_RFID_Reader_-_M6E_Nano1 = SparkFun Simultaneous RFID Reader - M6E Nano [part_number=SEN-14066]
  U1 = LIPO-2000mAh [package=lipo-2000]  # not connected
  U2 = LIPO-2000mAh [package=lipo-2000]  # not connected
  S1 = Toggle Switch [package=THT]
  Part3 = Adafruit PowerBoost 1000C [part_number="Adafruit #2465"]

nets:
  3V3: Raspberry_Pi_Zero1.3v3, SparkFun_Simultaneous_RFID_Reader_-_M6E_Nano1.VCC
  GND: Raspberry_Pi_Zero1.GND, SparkFun_Simultaneous_RFID_Reader_-_M6E_Nano1.GND, S1.L1, Part3.GND
  N1: Raspberry_Pi_Zero1.GPIO15, SparkFun_Simultaneous_RFID_Reader_-_M6E_Nano1.RX
  N2: Raspberry_Pi_Zero1.GPIO14, SparkFun_Simultaneous_RFID_Reader_-_M6E_Nano1.TX
  N3: Raspberry_Pi_Zero1.5V, Part3.5.0V
  N4: S1.COM, Part3.ENABLE
  N5: S1.L2, Part3.VBAT

custom parts:
  SparkFun Simultaneous RFID Reader - M6E Nano: Description: The SparkFun Simultaneous RFID Reader is an Arduino-compatible board to get you started with the M6E Nano UHF RFID Reader. Radio Frequency Identification (RFID) is becoming popular everywhere for tracking practically everything. Whether you want to get started by adding an RFID reader on your toolbox with tags on all your tools or allowing access to the tree house for your secret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
  Adafruit PowerBoost 1000C: PowerBoost 1000C is the perfect power supply for your portable project! With a built-in load-sharing battery charger circuit, you'll be able to keep your power-hungry project running even while recharging the battery! This little DC/DC boost converter module can be powered by any 3.7V LiIon/LiPoly battery, and convert the battery output to 5.2V DC for running your 5V projects.
